# Fritzing sketch Transmitter (saved by Fritzing 0.9.10b)
breadboards: 1

parts:
  Part1 = Arduino Nano (Rev3.0)
  RE1 = KY-040 Rotary encoder [package=THT]
  VCC1 = Battery block 9V
  M1 = NRF24L01-BO [package=THT]

nets:
  GND: Part1.GND, RE1.GND
  N1: Part1.D2, RE1.CLK
  N2: Part1.D3, RE1.DT
  N3: Part1.D4, RE1.SW
  N4: Part1.D7, M1.CE
  N5: Part1.D8, M1.CSN
  N6: Part1.D11/MOSI, M1.M0
  N7: Part1.D12/MISO, M1.M1
  5V: Part1.5V, RE1.Vcc
  N8: Part1.D13/SCK, M1.SCK
  N9: VCC1.-, M1.GND
  N10: VCC1.+, M1.VCC

custom parts:
  KY-040 Rotary encoder: KY-040 Rotary Encoder with switch on breakout borad from AZ Delivery
  Battery block 9V: 9 Volt battery block with 200mil pcb footprint spacing and large connection pads
  NRF24L01-BO: NRF24L01-BO breakout board for the NRF24L01. Pcb view suppressed as unneeded.
